// Logisim project PROJETO CC.circ as structural Verilog
module PROJETO_CC (
  input  A,
  input  B,
  output VERDE_RUA_A,
  output AMARELA_RUA_A,
  output VERMELHO_RUA_A,
  output VERDE_RUA_B,
  output AMARELO_RUA_B,
  output VERMELHO_RUA_B,
  output VERDE_PEDESTRE_RUA_A,
  output VERMELHO_PEDESTRE_RUA_A,
  output VERDE_PEDESTRE_RUA_B,
  output VERMELHO_PEDESTRE_RUA_B
);

  wire not_1_out, not_2_out, not_3_out, not_4_out;

  not not_1 (not_1_out, A);
  not not_2 (not_2_out, B);
  not not_3 (not_3_out, A);
  not not_4 (not_4_out, B);
  and and_1 (AMARELO_RUA_B, A, B);
  not not_5 (VERMELHO_RUA_B, A);
  not not_6 (VERMELHO_PEDESTRE_RUA_A, A);
  not not_7 (VERDE_PEDESTRE_RUA_B, A);
  and and_2 (VERDE_RUA_A, not_1_out, not_2_out);
  and and_3 (AMARELA_RUA_A, not_3_out, B);
  and and_4 (VERDE_RUA_B, A, not_4_out);

  assign VERDE_PEDESTRE_RUA_A = A;
  assign VERMELHO_PEDESTRE_RUA_B = A;
  assign VERMELHO_RUA_A = A;
endmodule

module PRJETO_CC (
  input  A,
  input  B
);

  wire and_1_out, and_2_out, and_3_out, and_4_out, not_1_out, not_2_out, not_3_out, not_4_out, not_5_out,
       not_6_out, not_7_out;

  not not_1 (not_1_out, A);
  not not_2 (not_2_out, B);
  not not_3 (not_3_out, A);
  not not_4 (not_4_out, B);
  and and_1 (and_1_out, A, B);
  not not_5 (not_5_out, A);
  not not_6 (not_6_out, A);
  not not_7 (not_7_out, A);
  and and_2 (and_2_out, not_1_out, not_2_out);
  LED led_1 (.in(and_2_out));
  LED led_2 (.in(and_3_out));
  and and_3 (and_3_out, not_3_out, B);
  LED led_3 (.in(A));
  and and_4 (and_4_out, A, not_4_out);
  LED led_4 (.in(and_4_out));
  LED led_5 (.in(and_1_out));
  LED led_6 (.in(not_5_out));
  LED led_7 (.in(A));
  LED led_8 (.in(not_6_out));
  LED led_9 (.in(not_7_out));
  LED led_10 (.in(A));

  // Notes on the sheet:
  //                              AMARELO RUA A
  //     VERDE RUA A
  //                 VEMELHO RUA A
  //   VERDE RUA B
  //         AMARELO RUA B
  //                   VERMELHO RUA B
  //   VERDE PEDESTRE RUA A
  //   VERMELHO PEDESTRE RUA A
  //   VERDE PEDESTRE RUA B
  //   VERMELHO PEDESTRE RUA B
endmodule
